// Logisim project 1 Bit ALU.circ as structural Verilog: 1 circuit, main circuit main
module main (
  input  Operand_B,
  input  Operand_A,
  input  Carry_IN,
  input  [2:0] ALU_Operation,
  input  Invert_B,
  output Result,
  output Carry
);

  wire adder_1_cout, adder_1_out, AND_2_out, AND_out, multiplexer_1_out, NAND_out, NOR_out, not_1_out, OR_out;

  Multiplexer #(.enable("false")) multiplexer_1 (
    .in0(Operand_B), .in1(not_1_out), .out(multiplexer_1_out), .sel(Invert_B));
  not not_1 (not_1_out, Operand_B);
  Adder #(.width(1)) adder_1 (
    .a(Operand_A), .b(multiplexer_1_out), .out(adder_1_out), .cin(Carry_IN), .cout(adder_1_cout));
  and AND (AND_out, ~ALU_Operation[0], ~ALU_Operation[1], ALU_Operation[2]);  // AND_Gate
  and AND_2 (AND_2_out, Operand_A, Operand_B);
  or OR (OR_out, Operand_A, Operand_B);
  nand NAND (NAND_out, Operand_A, Operand_B);
  nor NOR (NOR_out, Operand_A, Operand_B);
  and AND_3 (Carry, adder_1_cout, AND_out);
  Multiplexer #(.select(3), .enable("false")) multiplexer_2 (
    .in0(AND_2_out), .in1(OR_out), .in2(NAND_out), .in3(NOR_out), .in4(adder_1_out), .in5(1'b0), .in6(1'b0),
    .in7(1'b0), .out(Result), .sel(ALU_Operation));

  // Other names for the same wires on the sheet: ALUOpp[2:0] = ALU_Operation

  // Notes on the sheet:
  //   1 BIT ALU
  //   Defult Zero
endmodule
