// Logisim project 22 Bit ALU CU.circ as structural Verilog: 1 circuit, main circuit main
module main (
  input  [3:0] Operation,
  input  [2:0] ALUOpp,
  output [3:0] ALUOperation,
  output [1:0] MUXControl
);

  wire [3:0] multiplexer_1_out;

  Multiplexer #(.width(4), .enable("false")) multiplexer_1 (
    .in0(4'b0100), .in1(4'b1100), .out(multiplexer_1_out), .sel(ALUOpp[2]));
  Multiplexer #(.select(2), .width(4), .enable("false")) multiplexer_2 (
    .in0(4'b0100), .in1(4'b1100), .in2(Operation), .in3(multiplexer_1_out), .out(ALUOperation),
    .sel(ALUOpp[1:0]));
  Multiplexer #(.width(2), .enable("false")) multiplexer_3 (
    .in0(2'b00), .in1(ALUOperation[1:0]), .out(MUXControl), .sel(ALUOperation[2]));

  // Other names for the same wires on the sheet: _2ndOpp[3:0] = ALUOperation

  // Notes on the sheet:
  //   SLT/SRL/SLL
  //   ALU Control
  //   BEQ/BNE
  //   001
  //   010
  //   R-Type
  //   ADDi
  //   100
  //   SUBi
  //   111
endmodule
