// Logisim project 22 Bit ALU.circ as structural Verilog: 1 circuit, main circuit main
module main (
  input  [3:0] Operation,
  input  [4:0] ShiftValue,
  input  [1:0] MUXControl,
  input  [21:0] Operand_B,
  input  [21:0] Operand_A,
  output Zero_Flag,
  output [21:0] Result,
  output Carry_OUT,
  output OverFlow
);

  wire comparator_1_lt, main_1_carry, main_2_carry, main_3_carry, main_4_carry, main_5_carry, main_6_carry,
       main_7_carry, main_8_carry, main_9_carry, main_10_carry, main_11_carry, main_12_carry, main_13_carry,
       main_14_carry, main_15_carry, main_16_carry, main_17_carry, main_18_carry, main_20_carry,
       main_21_carry, main_22_carry;
  wire [21:0] ALUResult, LeftShiftResult, RightShiftResult, SLTResult;

  _1_Bit_ALU_main main_1 (
    .Result(ALUResult[0]), .Carry(main_1_carry), .Operand_B(Operand_B[0]), .Operand_A(Operand_A[0]),
    .Carry_IN(Operation[3]), .ALU_Operation(Operation[2:0]), .Invert_B(Operation[3]));
  _1_Bit_ALU_main main_2 (
    .Result(ALUResult[6]), .Carry(main_2_carry), .Operand_B(Operand_B[6]), .Operand_A(Operand_A[6]),
    .Carry_IN(main_20_carry), .ALU_Operation(Operation[2:0]), .Invert_B(Operation[3]));
  _1_Bit_ALU_main main_3 (
    .Result(ALUResult[12]), .Carry(main_3_carry), .Operand_B(Operand_B[12]), .Operand_A(Operand_A[12]),
    .Carry_IN(main_21_carry), .ALU_Operation(Operation[2:0]), .Invert_B(Operation[3]));
  _1_Bit_ALU_main main_4 (
    .Result(ALUResult[1]), .Carry(main_4_carry), .Operand_B(Operand_B[1]), .Operand_A(Operand_A[1]),
    .Carry_IN(main_1_carry), .ALU_Operation(Operation[2:0]), .Invert_B(Operation[3]));
  _1_Bit_ALU_main main_5 (
    .Result(ALUResult[7]), .Carry(main_5_carry), .Operand_B(Operand_B[7]), .Operand_A(Operand_A[7]),
    .Carry_IN(main_2_carry), .ALU_Operation(Operation[2:0]), .Invert_B(Operation[3]));
  _1_Bit_ALU_main main_6 (
    .Result(ALUResult[13]), .Carry(main_6_carry), .Operand_B(Operand_B[13]), .Operand_A(Operand_A[13]),
    .Carry_IN(main_3_carry), .ALU_Operation(Operation[2:0]), .Invert_B(Operation[3]));
  _1_Bit_ALU_main main_7 (
    .Result(ALUResult[18]), .Carry(main_7_carry), .Operand_B(Operand_B[18]), .Operand_A(Operand_A[18]),
    .Carry_IN(main_22_carry), .ALU_Operation(Operation[2:0]), .Invert_B(Operation[3]));
  _1_Bit_ALU_main main_8 (
    .Result(ALUResult[2]), .Carry(main_8_carry), .Operand_B(Operand_B[2]), .Operand_A(Operand_A[2]),
    .Carry_IN(main_4_carry), .ALU_Operation(Operation[2:0]), .Invert_B(Operation[3]));
  _1_Bit_ALU_main main_9 (
    .Result(ALUResult[8]), .Carry(main_9_carry), .Operand_B(Operand_B[8]), .Operand_A(Operand_A[8]),
    .Carry_IN(main_5_carry), .ALU_Operation(Operation[2:0]), .Invert_B(Operation[3]));
  _1_Bit_ALU_main main_10 (
    .Result(ALUResult[14]), .Carry(main_10_carry), .Operand_B(Operand_B[14]), .Operand_A(Operand_A[14]),
    .Carry_IN(main_6_carry), .ALU_Operation(Operation[2:0]), .Invert_B(Operation[3]));
  _1_Bit_ALU_main main_11 (
    .Result(ALUResult[19]), .Carry(main_11_carry), .Operand_B(Operand_B[19]), .Operand_A(Operand_A[19]),
    .Carry_IN(main_7_carry), .ALU_Operation(Operation[2:0]), .Invert_B(Operation[3]));
  _1_Bit_ALU_main main_12 (
    .Result(ALUResult[3]), .Carry(main_12_carry), .Operand_B(Operand_B[3]), .Operand_A(Operand_A[3]),
    .Carry_IN(main_8_carry), .ALU_Operation(Operation[2:0]), .Invert_B(Operation[3]));
  _1_Bit_ALU_main main_13 (
    .Result(ALUResult[9]), .Carry(main_13_carry), .Operand_B(Operand_B[9]), .Operand_A(Operand_A[9]),
    .Carry_IN(main_9_carry), .ALU_Operation(Operation[2:0]), .Invert_B(Operation[3]));
  _1_Bit_ALU_main main_14 (
    .Result(ALUResult[15]), .Carry(main_14_carry), .Operand_B(Operand_B[15]), .Operand_A(Operand_A[15]),
    .Carry_IN(main_10_carry), .ALU_Operation(Operation[2:0]), .Invert_B(Operation[3]));
  _1_Bit_ALU_main main_15 (
    .Result(ALUResult[20]), .Carry(main_15_carry), .Operand_B(Operand_B[20]), .Operand_A(Operand_A[20]),
    .Carry_IN(main_11_carry), .ALU_Operation(Operation[2:0]), .Invert_B(Operation[3]));
  _1_Bit_ALU_main main_16 (
    .Result(ALUResult[4]), .Carry(main_16_carry), .Operand_B(Operand_B[4]), .Operand_A(Operand_A[4]),
    .Carry_IN(main_12_carry), .ALU_Operation(Operation[2:0]), .Invert_B(Operation[3]));
  _1_Bit_ALU_main main_17 (
    .Result(ALUResult[10]), .Carry(main_17_carry), .Operand_B(Operand_B[10]), .Operand_A(Operand_A[10]),
    .Carry_IN(main_13_carry), .ALU_Operation(Operation[2:0]), .Invert_B(Operation[3]));
  _1_Bit_ALU_main main_18 (
    .Result(ALUResult[16]), .Carry(main_18_carry), .Operand_B(Operand_B[16]), .Operand_A(Operand_A[16]),
    .Carry_IN(main_14_carry), .ALU_Operation(Operation[2:0]), .Invert_B(Operation[3]));
  _1_Bit_ALU_main main_19 (
    .Result(ALUResult[21]), .Carry(Carry_OUT), .Operand_B(Operand_B[21]), .Operand_A(Operand_A[21]),
    .Carry_IN(main_15_carry), .ALU_Operation(Operation[2:0]), .Invert_B(Operation[3]));
  xor XNOR (OverFlow, Carry_OUT, main_15_carry);
  _1_Bit_ALU_main main_20 (
    .Result(ALUResult[5]), .Carry(main_20_carry), .Operand_B(Operand_B[5]), .Operand_A(Operand_A[5]),
    .Carry_IN(main_16_carry), .ALU_Operation(Operation[2:0]), .Invert_B(Operation[3]));
  _1_Bit_ALU_main main_21 (
    .Result(ALUResult[11]), .Carry(main_21_carry), .Operand_B(Operand_B[11]), .Operand_A(Operand_A[11]),
    .Carry_IN(main_17_carry), .ALU_Operation(Operation[2:0]), .Invert_B(Operation[3]));
  _1_Bit_ALU_main main_22 (
    .Result(ALUResult[17]), .Carry(main_22_carry), .Operand_B(Operand_B[17]), .Operand_A(Operand_A[17]),
    .Carry_IN(main_18_carry), .ALU_Operation(Operation[2:0]), .Invert_B(Operation[3]));
  Comparator #(.width(22), .mode("unsigned")) comparator_1 (
    .a(Operand_A), .b(Operand_B), .lt(comparator_1_lt));  // open: gt, eq
  Shifter #(.width(22), .shift("lr")) shifter_1 (.in(Operand_A), .\dist (ShiftValue), .out(RightShiftResult));
  Shifter #(.width(22)) shifter_2 (.in(Operand_A), .\dist (ShiftValue), .out(LeftShiftResult));
  Multiplexer #(.width(22), .enable("false")) multiplexer_1 (
    .in0({22{1'b0}}), .in1(22'h1), .out(SLTResult), .sel(comparator_1_lt));
  nor NOR (Zero_Flag, ALUResult[21], ALUResult[20], ALUResult[19], ALUResult[18], ALUResult[17], ALUResult[16], ALUResult[15], ALUResult[14], ALUResult[13], ALUResult[12], ALUResult[11], ALUResult[10], ALUResult[9], ALUResult[8], ALUResult[7], ALUResult[6], ALUResult[5], ALUResult[4], ALUResult[3], ALUResult[2], ALUResult[1], ALUResult[0]);
  Multiplexer #(.select(2), .width(22), .enable("false")) multiplexer_2 (
    .in0(ALUResult), .in1(LeftShiftResult), .in2(RightShiftResult), .in3(SLTResult), .out(Result),
    .sel(MUXControl));

  // Other names for the same wires on the sheet: R00 = ALUResult[0]; R01 = ALUResult[1]; R02 = ALUResult[2];
  //   R03 = ALUResult[3]; R04 = ALUResult[4]; R05 = ALUResult[5]; R06 = ALUResult[6]; R07 = ALUResult[7];
  //   R08 = ALUResult[8]; R09 = ALUResult[9]; R10 = ALUResult[10]; R11 = ALUResult[11]; R12 = ALUResult[12];
  //   R13 = ALUResult[13]; R14 = ALUResult[14]; R15 = ALUResult[15]; R16 = ALUResult[16]; R17 = ALUResult[17];
  //   R18 = ALUResult[18]; R19 = ALUResult[19]; R20 = ALUResult[20]; R21 = ALUResult[21]; A00 = Operand_A[0];
  //   A01 = Operand_A[1]; A02 = Operand_A[2]; A03 = Operand_A[3]; A04 = Operand_A[4]; A05 = Operand_A[5];
  //   A06 = Operand_A[6]; A07 = Operand_A[7]; A08 = Operand_A[8]; A09 = Operand_A[9]; A10 = Operand_A[10];
  //   A11 = Operand_A[11]; A12 = Operand_A[12]; A13 = Operand_A[13]; A14 = Operand_A[14]; A15 = Operand_A[15];
  //   A16 = Operand_A[16]; A17 = Operand_A[17]; A18 = Operand_A[18]; A19 = Operand_A[19]; A20 = Operand_A[20];
  //   A21 = Operand_A[21]; B00 = Operand_B[0]; B01 = Operand_B[1]; B02 = Operand_B[2]; B03 = Operand_B[3];
  //   B04 = Operand_B[4]; B05 = Operand_B[5]; B06 = Operand_B[6]; B07 = Operand_B[7]; B08 = Operand_B[8];
  //   B09 = Operand_B[9]; B10 = Operand_B[10]; B11 = Operand_B[11]; B12 = Operand_B[12]; B13 = Operand_B[13];
  //   B14 = Operand_B[14]; B15 = Operand_B[15]; B16 = Operand_B[16]; B17 = Operand_B[17]; B18 = Operand_B[18];
  //   B19 = Operand_B[19]; B20 = Operand_B[20]; B21 = Operand_B[21]

  // Notes on the sheet:
  //   Invert B
  //   Carry IN
  //   Select Bit (Operation)
  //   Output Tunnels
  //   SLT Operation
  //   Right Shift
  //   Left Shift
  //   SRL/SLL Operation
  //   Output MUX
endmodule
