// Logisim project 22 Bit Control Unit.circ as structural Verilog: 1 circuit, main circuit main
module main (
  input  [3:0] Operation_Code,
  output JUMP,
  output Branch,
  output MemToReg,
  output RegWrite,
  output RegDst,
  output MemRead,
  output MemWrite,
  output ALUSrc,
  output [2:0] ALUOpp
);

  wire ADDi_out, BEQ_out, BNE_out, SUBi_out;
  wire [1:0] OR_2_out;

  and R_Type (RegDst, ~Operation_Code[3], ~Operation_Code[2], ~Operation_Code[1], ~Operation_Code[0]);  // AND_Gate
  and LW (MemRead, ~Operation_Code[3], ~Operation_Code[2], Operation_Code[1], Operation_Code[0]);  // AND_Gate
  and SW (MemWrite, ~Operation_Code[3], Operation_Code[2], ~Operation_Code[1], ~Operation_Code[0]);  // AND_Gate
  and ADDi (ADDi_out, ~Operation_Code[3], Operation_Code[2], ~Operation_Code[1], Operation_Code[0]);  // AND_Gate
  and SUBi (SUBi_out, ~Operation_Code[3], Operation_Code[2], Operation_Code[1], ~Operation_Code[0]);  // AND_Gate
  or OR (OR_2_out[1], ADDi_out, RegDst);
  and BEQ (BEQ_out, ~Operation_Code[3], Operation_Code[2], Operation_Code[1], Operation_Code[0]);  // AND_Gate
  and BNE (BNE_out, Operation_Code[3], ~Operation_Code[2], ~Operation_Code[1], ~Operation_Code[0]);  // AND_Gate
  or OR_2 (OR_2_out[0], ADDi_out, BEQ_out, BNE_out);
  and u_JUMP (JUMP, Operation_Code[3], Operation_Code[2], Operation_Code[1], Operation_Code[0]);
  or OR_3 (Branch, BNE_out, BEQ_out);
  or OR_4 (RegWrite, SUBi_out, ADDi_out, MemRead, RegDst);
  or OR_5 (ALUSrc, SUBi_out, ADDi_out, MemWrite, MemRead);
  Multiplexer #(.width(3), .enable("false")) multiplexer_1 (
    .in0({1'b0, OR_2_out}), .in1(3'b111), .out(ALUOpp), .sel(SUBi_out));

  assign MemToReg = MemRead;

  // Notes on the sheet:
  //   Control Unit
endmodule
