// Logisim project 22 Bit Mips.circ as structural Verilog: 1 circuit, main circuit main
module main (
  output OverFlow,
  output CarryOut,
  output ZeroFlag
);

  wire ALUSrc, Branch, CLK, CLR_RAM, CLR_REG, Jump, MemRead, MemToReg, MemWrite, RegDst, RegWrite, Reset_out;
  wire [1:0] main_4_muxcontrol;
  wire [2:0] _09_11, _12_14, _15_17, ALUOpp, multiplexer_1_out;
  wire [3:0] _00_03, _18_21, main_4_aluoperation;
  wire [4:0] _04_08;
  wire [21:0] IMValue, J_B_Adress, main_2_data_1, main_2_data_2, main_5_result, multiplexer_2_out,
       multiplexer_3_out, PCA, ram_1_data, register_1_q;

  Clock u_CLK (.out(CLK));
  Button REG_Clear (.out(CLR_REG));
  Button RAM_Clear (.out(CLR_RAM));
  Register #(.width(22)) register_1 (.D(J_B_Adress), .Q(register_1_q), .clk(CLK), .clr(Reset_out));  // open: en
  Button Reset (.out(Reset_out));
  Adder #(.width(22)) adder_1 (.a(22'h1), .b(register_1_q), .out(PCA));  // open: cin, cout
  ROM #(.addrWidth(22), .dataWidth(22)) rom_1 (
    .addr(register_1_q), .data({_18_21, _15_17, _12_14, _09_11, _04_08, _00_03}));  // open: sel
  _22_Bit_Control_Unit_main main_1 (
    .Operation_Code(_18_21), .JUMP(Jump), .Branch(Branch), .MemToReg(MemToReg), .RegWrite(RegWrite),
    .RegDst(RegDst), .MemRead(MemRead), .MemWrite(MemWrite), .ALUSrc(ALUSrc), .ALUOpp(ALUOpp));
  Multiplexer #(.width(3), .enable("false")) multiplexer_1 (
    .in0(_12_14), .in1(_09_11), .out(multiplexer_1_out), .sel(RegDst));
  assign IMValue = {{10{_09_11[2]}}, {_09_11, _04_08, _00_03}};  // Bit_Extender bit_extender_1
  _22_Bit_Register_file_main main_2 (
    .Data_In(multiplexer_3_out), .Reg_W(RegWrite), .Data_Address(multiplexer_1_out), .Data_1(main_2_data_1),
    .RS(_15_17), .Data_2(main_2_data_2), .RT(_12_14), .CLK(CLK), .CLR(CLR_REG));
  Jump___Branch_main main_3 (
    .PCAdder_18_21(PCA[21:18]), .PCAdder(PCA), .Result(J_B_Adress),
    .Code_0_17({_15_17, _12_14, _09_11, _04_08, _00_03}), .ImmediateValue(IMValue), .Jump(Jump),
    .Branch(Branch), .ZeroFlag(ZeroFlag), .Beq_Bnq(_18_21[3]));
  Multiplexer #(.width(22), .enable("false")) multiplexer_2 (
    .in0(main_2_data_2), .in1(IMValue), .out(multiplexer_2_out), .sel(ALUSrc));
  _22_Bit_ALU_CU_main main_4 (
    .ALUOperation(main_4_aluoperation), .Operation(_00_03), .ALUOpp(ALUOpp), .MUXControl(main_4_muxcontrol));
  _22_Bit_ALU_main main_5 (
    .Zero_Flag(ZeroFlag), .Result(main_5_result), .Carry_OUT(CarryOut), .OverFlow(OverFlow),
    .Operation(main_4_aluoperation), .ShiftValue(_04_08), .MUXControl(main_4_muxcontrol),
    .Operand_B(multiplexer_2_out), .Operand_A(main_2_data_1));
  RAM #(.addrWidth(22), .dataWidth(22), .bus("separate")) ram_1 (
    .addr(main_5_result), .din(main_2_data_2), .data(ram_1_data), .str(MemWrite), .clk(CLK), .ld(MemRead),
    .clr(CLR_RAM));  // open: sel
  Multiplexer #(.width(22), .enable("false")) multiplexer_3 (
    .in0(main_5_result), .in1(ram_1_data), .out(multiplexer_3_out), .sel(MemToReg));

  // Other names for the same wires on the sheet: PCA_18_21[3:0] = PCA[21:18]

  // Notes on the sheet:
  //   172 1625 042 ---------- Ekhfa Hossain
  //   172 1489 042 ---------- Sudipta Mandal
  //   contents of rom_1 (hex, n*v repeats v):
  //   0 141006 101002 c2002 191003 101001 0 1d1002 149003 3c0007 0 0 211002 189001 3c000c 3c0000
  //   22 BIT MIPS ARCHITECTURE
  //   Immediate Value (0-11)
  //   BEQ/BNE
  //   21 no. bit only
endmodule
