// Logisim project 22 Bit Register-file.circ as structural Verilog: 1 circuit, main circuit main
module main (
  input  [21:0] Data_In,
  input  [2:0] RS,
  input  [2:0] RT,
  input  Reg_W,
  input  CLK,
  input  CLR,
  input  [2:0] Data_Address,
  output [21:0] Data_1,
  output [21:0] Data_2
);

  wire demultiplexer_1_out0, demultiplexer_1_out1, demultiplexer_1_out2, demultiplexer_1_out3,
       demultiplexer_1_out4, demultiplexer_1_out5, demultiplexer_1_out6, demultiplexer_1_out7;
  wire [21:0] register_1_q, register_2_q, register_3_q, register_4_q, register_5_q, register_6_q,
       register_7_q, register_8_q;

  Demultiplexer #(.select(3), .enable("false")) demultiplexer_1 (
    .out0(demultiplexer_1_out0), .out1(demultiplexer_1_out1), .out2(demultiplexer_1_out2),
    .out3(demultiplexer_1_out3), .out4(demultiplexer_1_out4), .out5(demultiplexer_1_out5),
    .out6(demultiplexer_1_out6), .out7(demultiplexer_1_out7), .in(Reg_W), .sel(Data_Address));
  Register #(.width(22)) register_1 (.D(Data_In), .en(demultiplexer_1_out0), .Q(register_1_q), .clk(CLK), .clr(CLR));
  Register #(.width(22)) register_2 (.D(Data_In), .en(demultiplexer_1_out1), .Q(register_2_q), .clk(CLK), .clr(CLR));
  Register #(.width(22)) register_3 (.D(Data_In), .en(demultiplexer_1_out2), .Q(register_3_q), .clk(CLK), .clr(CLR));
  Register #(.width(22)) register_4 (.D(Data_In), .en(demultiplexer_1_out3), .Q(register_4_q), .clk(CLK), .clr(CLR));
  Register #(.width(22)) register_5 (.D(Data_In), .en(demultiplexer_1_out4), .Q(register_5_q), .clk(CLK), .clr(CLR));
  Register #(.width(22)) register_6 (.D(Data_In), .en(demultiplexer_1_out5), .Q(register_6_q), .clk(CLK), .clr(CLR));
  Register #(.width(22)) register_7 (.D(Data_In), .en(demultiplexer_1_out6), .Q(register_7_q), .clk(CLK), .clr(CLR));
  Register #(.width(22)) register_8 (.D(Data_In), .en(demultiplexer_1_out7), .Q(register_8_q), .clk(CLK), .clr(CLR));
  Multiplexer #(.select(3), .width(22), .enable("false")) multiplexer_1 (
    .in0(register_1_q), .in1(register_2_q), .in2(register_3_q), .in3(register_4_q), .in4(register_5_q),
    .in5(register_6_q), .in6(register_7_q), .in7(register_8_q), .out(Data_1), .sel(RS));
  Multiplexer #(.select(3), .width(22), .enable("false")) multiplexer_2 (
    .in0(register_1_q), .in1(register_2_q), .in2(register_3_q), .in3(register_4_q), .in4(register_5_q),
    .in5(register_6_q), .in6(register_7_q), .in7(register_8_q), .out(Data_2), .sel(RT));

  // Notes on the sheet:
  //   R0
  //   R1
  //   R2
  //   R3
  //   R4
  //   R5
  //   R6
  //   R7
endmodule
