// Logisim project Jump & Branch.circ as structural Verilog: 1 circuit, main circuit main
module main (
  input  [3:0] PCAdder_18_21,
  input  [21:0] PCAdder,
  input  [17:0] Code_0_17,
  input  [21:0] ImmediateValue,
  input  Jump,
  input  Branch,
  input  ZeroFlag,
  input  Beq_Bnq,
  output [21:0] Result
);

  wire AND_2_out, AND_3_out, AND_4_out, AND_out, OR_out;
  wire [21:0] adder_1_out, multiplexer_1_out;

  Adder #(.width(22)) adder_1 (.a(PCAdder), .b(ImmediateValue), .out(adder_1_out));  // open: cin, cout
  and AND (AND_out, ZeroFlag, ~Beq_Bnq);  // AND_Gate
  and AND_2 (AND_2_out, Beq_Bnq, ~ZeroFlag);  // AND_Gate
  and AND_3 (AND_3_out, Branch, AND_2_out);
  and AND_4 (AND_4_out, Branch, AND_out);
  Multiplexer #(.width(22), .enable("false")) multiplexer_1 (
    .in0(PCAdder), .in1(adder_1_out), .out(multiplexer_1_out), .sel(OR_out));
  or OR (OR_out, AND_3_out, AND_4_out);
  Multiplexer #(.width(22), .enable("false")) multiplexer_2 (
    .in0(multiplexer_1_out), .in1({PCAdder_18_21, Code_0_17}), .out(Result), .sel(Jump));

  // Notes on the sheet:
  //   Jump & Branch
endmodule
